# Fritzing sketch esp32-main-board (saved by Fritzing 0.9.3b)
circuit board: 6.15928cm x 4.62532cm
perfboards: 1

parts:
  Q1 = NPN-Transistor [part_number=BC546 package="TO92 [THT]"]
  R1 = Photocell (LDR) [package=THT]
  MH-Z2 = MH-Z14 [part_number=MH-Z14]
  BME280 = BME280 Breakout
  NEOPIXEL1 = Neopixel Strip -- Black (30/m)
  SCL5V = female pin header, 2 pins [form="♀ (female)"]
  R5 = Resistor [tolerance=±5% resistance=10k package=THT]
  R6 = Resistor [tolerance=±5% resistance=10k package=THT]
  N-mos1 = mystery part, 3 pins [chip_label=N part_number=2N7000]
  R8 = Resistor [tolerance=±5% resistance=10k package=THT]
  N-mos2 = mystery part, 3 pins [chip_label=N part_number=2N7000]
  U1 = lolin
  BME280_data = female pin header, 2 pins [form="♀ (female)"]
  R7 = Resistor [tolerance=±5% resistance=10k package=THT]
  LCD_LED = female pin header, 2 pins [form="♀ (female)"]
  J1 = male pin header, 3 pins [form="♂ (male)"]
  J2 = male pin header, 3 pins [form="♂ (male)"]
  R10 = Resistor [tolerance=±5% resistance=10k package=THT]
  phototran = female pin header, 2 pins [form="♀ (female)"]
  phototran2 = female pin header, 2 pins [form="♀ (female)"]
  R11 = Photocell (LDR) [package=THT]
  LCD_I2C2 = LCD I2C [package="DIP (Dual Inline) [THT]"]
  PMS5003 = female pin header, 8 pins [form="♀ (female)"]
  ESP16b = female pin header, 16 pins [form="♀ (female)"]  # not connected
  ESP20b = female pin header, 20 pins [form="♀ (female)"]  # not connected
  C4 = Electrolytic Capacitor [capacitance=22µF voltage=16V package="100 mil [THT, electrolytic]"]
  PWR = Header 2 [package=jst-2-pth-ns]
  SDA5V = female pin header, 2 pins [form="♀ (female)"]
  R12 = Trimmer Potentiometer [maximum_resistance=10kΩ package=THT]
  R13 = Resistor [tolerance=±5% resistance=4.7k package=THT]
  3_3 = double row male pin header, 8 pins [form="♂ (male)"]
  Q2 = Basic FET P-Channel [package="TO220 [THT]"]
  R14 = Resistor [tolerance=±5% resistance=10k package=THT]

nets (from the schematic view):
  GND: Q1.E, MH-Z2.2, MH-Z2.3, BME280.GND, NEOPIXEL1.GND, U1.connector37, LCD_LED.pin1, LCD_I2C2.GND, PMS5003.pin2, C4.-, PWR.1
  N1: Q1.B, J1.pin2
  N2: Q1.C, LCD_LED.pin2, Q2.gate, R14.Pin_1
  N3: R1.pin_0, J1.pin1, phototran.pin1
  N4: R1.pin_1, J2.pin2, phototran.pin2
  5V: MH-Z2.1, MH-Z2.15, NEOPIXEL1.+5V, R5.Pin_0, R8.Pin_0, J2.pin1, LCD_I2C2.VCC, PMS5003.pin1, PWR.2, R14.Pin_0
  N5: MH-Z2.4, U1.connector2
  3.3V: BME280.3.3V, R6.Pin_0, N-mos1.pin2, N-mos2.pin2, U1.connector0, R7.Pin_0, J2.pin3, R10.Pin_0, C4.+
  N6: BME280.SDI/SDA, N-mos2.pin1, U1.connector32, BME280_data.pin1, R7.Pin_1
  N7: BME280.SCK/SCL, R6.Pin_1, N-mos1.pin1, U1.connector33, BME280_data.pin2
  N8: NEOPIXEL1.DI, U1.connector19
  N9: SCL5V.pin1, SCL5V.pin2, R5.Pin_1, N-mos1.pin3, LCD_I2C2.SCL
  N10: R8.Pin_1, N-mos2.pin3, LCD_I2C2.SDA, SDA5V.pin1, SDA5V.pin2
  N11: U1.connector8, R12.leg2
  N12: U1.connector17, phototran2.pin1, R11.pin_1
  N13: U1.connector22, PMS5003.pin3
  N14: U1.connector23, PMS5003.pin5
  N15: U1.connector24, PMS5003.pin4
  N16: J1.pin3, R13.Pin_0
  N17: R10.Pin_1, phototran2.pin2, R11.pin_0
  LCD LED2: LCD_I2C2.LED_1, Q2.source
  LCD LED1: LCD_I2C2.LED_2, Q2.drain
  N18: R12.wiper, R13.Pin_1
  N19: 3_3.pin1, 3_3.pin2, 3_3.pin3

notes:
  J1 - switch between -DAC- PWM(25) and phototransistor1
  J2 - switch between 3.3/5V for phototransistor1 - disconnected
  TODO:
  - piny 2 i 15 wolne - LEDs?

custom parts:
  MH-Z14: MH-Z14 NDIR Infrared gas module is a common type, small size sensor, using non-dispersive infrared (NDIR) principle to detect the existence of CO2 in the air, with good selectivity, non-oxygen dependant, long life. Built-in temperature sensor can do temperature compensation; and it has digital output and analog voltage output.
  Neopixel Strip -- Black (30/m): Neopixel Strip, Black, 30 pixels per meter.
