# Fritzing sketch gp2y10 (saved by Fritzing 0.9.3b)
circuit board: 1.82056cm x 4.27131cm
breadboards: 1

parts:
  C1 = Electrolytic Capacitor [capacitance=0.22mF package="100 mil [THT, electrolytic]"]
  Power_plug1 = Power plug
  ESP32_pins = female pin header, 2 pins [form="♀ (female)"]
  C2 = Electrolytic Capacitor [capacitance=0.1nF package="100 mil [THT, electrolytic]"]
  Q1 = NPN-Transistor [part_number=BC546 package="TO92 [THT]"]
  R2 = Resistor [tolerance=±1% resistance=2.2 package=THT]
  R3 = Resistor [tolerance=±1% resistance=3.3 package=THT]
  R4 = Resistor [tolerance=±1% resistance=4.7 package=THT]
  R1 = Resistor [tolerance=±1% resistance=150 package=THT]
  GP2Y10 = male pin header, 6 pins [form="♂ (male)"]
  ESP32 = male pin header, 2 pins [form="♂ (male)"]
  PWR = male pin header, 2 pins [form="♂ (male)"]

nets:
  N1: C1.-, Power_plug1.GND, C2.-, Q1.E, R3.Pin_1, GP2Y10.pin2, GP2Y10.pin4, PWR.pin2
  N2: C1.+, R1.Pin_1, GP2Y10.pin1
  N3: Power_plug1.VCC, C2.+, R1.Pin_0, GP2Y10.pin6, PWR.pin1
  N4: ESP32_pins.pin1, R2.Pin_1, R3.Pin_0, ESP32.pin1
  N5: ESP32_pins.pin2, R4.Pin_1, ESP32.pin2
  N6: Q1.B, R4.Pin_0
  N7: Q1.C, GP2Y10.pin3
  N8: R2.Pin_0, GP2Y10.pin5
